# Fritzing sketch MULTIWII_BOARD_v2 (saved by Fritzing 0.9.4)
circuit board: 4cm x 4cm
breadboards: 1

parts:
  RESET = Pushbutton [package="[THT]"]
  R1 = Resistor [tolerance=±5% resistance=10k package=THT]
  C4 = Electrolytic Capacitor [capacitance=10µF package="100 mil [THT, electrolytic]"]
  C5 = Ceramic Capacitor [capacitance=100nF package="100 mil [THT, multilayer]"]
  U1 = ATmega328 [package=tqfp]
  XTAL1 = Crystal [frequency="16 MHz" package=THT]
  C3 = Ceramic Capacitor [capacitance=100nF package="100 mil [THT, multilayer]"]
  C2 = Ceramic Capacitor [capacitance=22pF package="100 mil [THT, multilayer]"]
  Part2 = GY-88
  C1 = Ceramic Capacitor [capacitance=22pF package="100 mil [THT, multilayer]"]
  R6 = Resistor [tolerance=±5% resistance=10k package=THT]
  R7 = Resistor [tolerance=±5% resistance=22k package=THT]
  R8 = Trimmer Potentiometer [maximum_resistance=5kΩ package=THT]
  R5 = Resistor [tolerance=±5% resistance=51k package=THT]
  BAT = male pin header, 1 pin [form="♂ (male)"]
  C6 = Ceramic Capacitor [capacitance=100nF package="100 mil [THT, multilayer]"]
  RECEIVER = male pin header, 7 pins [form="♂ (male)"]
  MOTORS = male pin header, 6 pins [form="♂ (male)"]
  BUZ = male pin header, 2 pins [form="♂ (male)"]
  PRG = male pin header, 2 pins [form="♂ (male)"]
  FTDI = male pin header, 5 pins [form="♂ (male)"]

nets:
  reset: RESET.Pin_1, RESET.Pin_2, R1.Pin_0, C5.0, U1.PC6(_RESET)
  GND: RESET.Pin_3, RESET.Pin_4, C4.-, U1.GND, U1.AGND, C3.1, C2.1, Part2.GND, C1.1, R8.leg1, C6.0, RECEIVER.pin1, MOTORS.pin1, BUZ.pin1, FTDI.pin1
  5V/avcc: R1.Pin_1, C4.+, U1.VCC, U1.AVCC, C3.0, Part2.VCC, PRG.pin2, FTDI.pin2
  N1: C5.1, FTDI.pin5
  N2: U1.PD3(INT1), MOTORS.pin3
  N3: U1.PD4(XCK_T0), RECEIVER.pin4
  xlat1: U1.PB6(XTAL1_TOSC1), XTAL1.pin_1, C2.0
  xlat2: U1.PB7(XTAL2_TOSC2), XTAL1.pin_0, C1.0
  N4: U1.PD5(T1), RECEIVER.pin5
  N5: U1.PD6(AIN0), RECEIVER.pin6
  N6: U1.PD7(AIN1), RECEIVER.pin7
  N7: U1.PB0(ICP), BUZ.pin2
  N8: U1.PB1(OC1A), MOTORS.pin4
  N9: U1.PB2(SS_OC1B), MOTORS.pin5
  mosi: U1.PB3(MOSI_OC2), MOTORS.pin6
  miso: U1.PB4(MISO)
  sck: U1.PB5(SCK)
  aref: U1.AREF, C6.1
  vbat: U1.PC3(ADC3), R6.Pin_1, R5.Pin_0
  sda: U1.PC4(ADC4_SDA), Part2.SDA
  scl: U1.PC5(ADC5_SCL), Part2.SCL
  rxd: U1.PD0(RXD), FTDI.pin3
  txd: U1.PD1(TXD), FTDI.pin4
  N10: U1.PD2(INT0), RECEIVER.pin3
  N11: R6.Pin_0, R7.Pin_0
  N12: R7.Pin_1, R8.wiper
  12V: R5.Pin_1, BAT.pin1
  N13: RECEIVER.pin2, MOTORS.pin2, PRG.pin1

custom parts:
  GY-88: This IMU 10DOF is a motion tracking module. Its design is based on the sensor MPU6050,HMC5883L and BMP085.The sensor MPU6050 which is the world’s first integrated 6-axis Motion Tracking device, that combines a 3-axis gyroscope, 3-axis accelerometer, and a Digital Motion Processor™ (DMP).The Honeywell’s HMC5883L which is a 3-axis digital compass. The BMP085 is a high-accuracy chip to detect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
