# Fritzing sketch MULTIWII_BOARD_v3 (saved by Fritzing 0.9.4)
circuit board: 4cm x 4cm
breadboards: 1

parts:
  RESET = Pushbutton [package="[THT]"]
  U1 = ATmega328 [package=tqfp]
  BUZ = male pin header, 2 pins [form="♂ (male)"]
  FTDI = male pin header, 5 pins [form="♂ (male)"]
  XTAL1 = Crystal [frequency="16 MHz" package=SMD]
  C1 = Ceramic Capacitor [capacitance=22pF package="0805 [SMD, multilayer]"]
  C2 = Ceramic Capacitor [capacitance=22pF package="0805 [SMD, multilayer]"]
  C3 = Ceramic Capacitor [capacitance=100nF package="0805 [SMD, multilayer]"]
  C6 = Ceramic Capacitor [capacitance=100nF package="0805 [SMD, multilayer]"]
  MOTORS = Molex Picoblade Series Header [part_number=0532610619 package=Picoblade-53261-0619]
  RECEIVER = Molex Picoblade Series Header [part_number=0532610719 package=Picoblade-53261-0719]
  U2 = Voltage Regulator - 5V [package="DPak [SMD]"]
  C4 = Tantalum Capacitor [capacitance=1µF package="B 3528 [SMD, tantalum]"]
  C7 = Tantalum Capacitor [capacitance=10µF package="B 3528 [SMD, tantalum]"]
  C5 = Ceramic Capacitor [capacitance=100nF package="0805 [SMD, multilayer]"]
  R5 = Resistor [tolerance=±5% resistance=100k package="0805 [SMD]"]
  R6 = Resistor [tolerance=±5% resistance=47k package="0805 [SMD]"]
  R1 = Resistor [tolerance=±5% resistance=10k package="0805 [SMD]"]
  Part3 = InvenSense MPU6050
  Pad1 = Pad [width=1 height=1 connect=center]
  Pad2 = Pad [width=1 height=1 connect=center]

nets:
  reset: RESET.Pin_1, RESET.Pin_2, U1.PC6(_RESET), C5.0, R1.Pin_0
  GND: RESET.Pin_3, RESET.Pin_4, U1.GND, U1.AGND, BUZ.pin1, FTDI.pin1, C1.1, C2.1, C3.1, C6.0, MOTORS.1, RECEIVER.1, U2.GND, C4.-, C7.-, R6.Pin_0, Part3.GND
  N1: U1.PD3(INT1), MOTORS.3
  N2: U1.PD4(XCK_T0), RECEIVER.4
  5V/avcc: U1.VCC, U1.AVCC, FTDI.pin2, C3.0, RECEIVER.2, U2.output_voltage, C4.+, R1.Pin_1, Part3.VCC
  xlat1: U1.PB6(XTAL1_TOSC1), XTAL1.pin_1, C2.0
  xlat2: U1.PB7(XTAL2_TOSC2), XTAL1.pin_0, C1.0
  N3: U1.PD5(T1), RECEIVER.5
  N4: U1.PD6(AIN0), RECEIVER.6
  N5: U1.PD7(AIN1), RECEIVER.7
  N6: U1.PB0(ICP), BUZ.pin2
  N7: U1.PB1(OC1A), MOTORS.4
  N8: U1.PB2(SS_OC1B), MOTORS.5
  mosi: U1.PB3(MOSI_OC2), MOTORS.6
  miso: U1.PB4(MISO), Pad1.pad
  sck: U1.PB5(SCK), Pad2.pad
  aref: U1.AREF, C6.1
  vbat: U1.PC3(ADC3), R5.Pin_0, R6.Pin_1
  sda: U1.PC4(ADC4_SDA), Part3.SDA
  scl: U1.PC5(ADC5_SCL), Part3.SCL
  rxd: U1.PD0(RXD), FTDI.pin3
  txd: U1.PD1(TXD), FTDI.pin4
  N9: U1.PD2(INT0), RECEIVER.3
  N10: FTDI.pin5, C5.1
  12V: MOTORS.2, U2.input_voltage, C7.+, R5.Pin_1
