# Fritzing sketch POWER_BOARD_v1 (saved by Fritzing 0.9.4)
circuit board: 6cm x 6cm

parts:
  RESET = Pushbutton [package="[THT]"]
  R1 = Resistor [tolerance=±5% resistance=10k package=THT]
  C4 = Electrolytic Capacitor [capacitance=10µF package="100 mil [THT, electrolytic]"]
  U1 = ATmega328 [package=tqfp]
  C1 = Ceramic Capacitor [capacitance=22pF package="100 mil [THT, multilayer]"]
  C2 = Ceramic Capacitor [capacitance=22pF package="100 mil [THT, multilayer]"]
  M1 = male pin header, 3 pins [form="♂ (male)"]
  M2 = male pin header, 3 pins [form="♂ (male)"]
  M4 = male pin header, 3 pins [form="♂ (male)"]
  M3 = male pin header, 3 pins [form="♂ (male)"]
  PRG = male pin header, 2 pins [form="♂ (male)"]
  RECEIVER = male pin header, 10 pins [form="♂ (male)"]
  FTDI = male pin header, 5 pins [form="♂ (male)"]
  PPM = male pin header, 1 pin [form="♂ (male)"]
  FC = male pin header, 6 pins [form="♂ (male)"]
  Pad1 = Pad [width=1.1653867294856681 height=1.170600706713777 connect=center]
  Pad2 = Pad [width=1.1653867294856681 height=1.170600706713777 connect=center]
  MAG = female pin header, 4 pins [form="♀ (female)"]
  FC_I2C = female pin header, 3 pins [form="♀ (female)"]
  BAR = female pin header, 4 pins [form="♀ (female)"]
  XTAL1 = Crystal [frequency="16 MHz" package=THT]
  C6 = Ceramic Capacitor [capacitance=100nF package="200 mil [THT, multilayer]"]
  C3 = Ceramic Capacitor [capacitance=100nF package="200 mil [THT, multilayer]"]
  C5 = Ceramic Capacitor [capacitance=100nF package="200 mil [THT, multilayer]"]

nets:
  reset: RESET.Pin_1, RESET.Pin_2, R1.Pin_0, U1.PC6(_RESET), C5.0
  GND: RESET.Pin_3, RESET.Pin_4, C4.-, U1.GND, U1.AGND, C1.1, C2.1, M1.pin1, M2.pin1, M4.pin1, M3.pin1, RECEIVER.pin1, FTDI.pin1, FC.pin1, MAG.pin2, BAR.pin2, C6.1, C3.1
  5V/avcc: R1.Pin_1, C4.+, U1.VCC, U1.AVCC, PRG.pin1, FTDI.pin2, C3.0
  ch7: U1.PD4(XCK_T0), RECEIVER.pin9
  xlat1: U1.PB6(XTAL1_TOSC1), C2.0, XTAL1.pin_1
  xlat2: U1.PB7(XTAL2_TOSC2), C1.0, XTAL1.pin_0
  ch6: U1.PD5(T1), RECEIVER.pin8
  ch5: U1.PD6(AIN0), RECEIVER.pin7
  ch4: U1.PD7(AIN1), RECEIVER.pin6
  ch3: U1.PB0(ICP), RECEIVER.pin5
  ch2: U1.PB1(OC1A), RECEIVER.pin4
  ppm: U1.PB2(SS_OC1B), PPM.pin1
  ch1: U1.PB3(MOSI_OC2), RECEIVER.pin3
  N1: U1.PB4(MISO), Pad2.pad
  N2: U1.PB5(SCK), Pad1.pad
  aref: U1.AREF, C6.0
  rdx: U1.PD0(RXD), FTDI.pin3
  txd: U1.PD1(TXD), FTDI.pin4
  ch8: U1.PD2(INT0), RECEIVER.pin10
  5.1V: M1.pin2, M2.pin2, M4.pin2, M3.pin2, PRG.pin2, RECEIVER.pin2, FC.pin2
  N3: M1.pin3, FC.pin3
  N4: M2.pin3, FC.pin4
  N5: M4.pin3, FC.pin5
  N6: M3.pin3, FC.pin6
  N7: FTDI.pin5, C5.1
  3.3V: MAG.pin1, FC_I2C.pin1, BAR.pin1
  N8: MAG.pin3, FC_I2C.pin2, BAR.pin3
  N9: MAG.pin4, FC_I2C.pin3, BAR.pin4
